# Fritzing sketch layout (saved by Fritzing 1.0.7)

parts:
  J1 = STM32 Nucleo boards
  Composant1 = BME280 Breakout

nets:
  N1: J1.A4/SDA, Composant1.SDI/SDA
  N2: J1.A5/SCL, Composant1.SCK/SCL
  3V3: J1.3V3, Composant1.3.3V
  GND: J1.GND, Composant1.GND
